// Logisim project a6.circ as structural Verilog: 1 circuit, main circuit main
module main (
  input  in_1,
  input  left_input,
  input  in_3,
  input  in_4,
  input  in_5,
  input  in_6,
  input  in_7,
  input  in_8,
  input  in_9,
  output out_10,
  output out_11,
  output out_12,
  output out_13,
  output out_14,
  output out_15,
  output out_16
);

  wire and_1_out, and_2_out, and_3_out, and_4_out, and_5_out, and_6_out, and_7_out, and_8_out, and_9_out,
       and_10_out, and_11_out, and_12_out, and_13_out, and_14_out, and_15_out, and_16_out, and_17_out,
       and_18_out, and_19_out, clock_1_out, d_ff_1_q, d_ff_2_q, d_ff_3_q, d_ff_6_q, d_ff_8_q, d_ff_10_q,
       d_ff_11_q, d_ff_12_q, d_ff_13_q, not_1_out, not_2_out, not_3_out, not_4_out, not_5_out, not_6_out,
       not_7_out, not_8_out, not_9_out, not_10_out, not_11_out, not_12_out, or_1_out, or_2_out, or_3_out,
       or_4_out, or_5_out, or_6_out, or_7_out, or_8_out, xor_1_out, xor_2_out, xor_3_out, xor_4_out,
       xor_5_out, xor_6_out, xor_7_out, xor_8_out, xor_9_out, xor_10_out, xor_11_out;

  Clock clock_1 (.out(clock_1_out));
  D_Flip_Flop d_ff_1 (.D(in_9), .clk(clock_1_out), .Q(d_ff_1_q));  // open: Qn, preset, reset
  and and_1 (and_1_out, d_ff_2_q, or_3_out);
  D_Flip_Flop d_ff_2 (.D(in_8), .clk(clock_1_out), .Q(d_ff_2_q));  // open: Qn, preset, reset
  not not_1 (not_1_out, d_ff_1_q);
  and and_2 (and_2_out, or_2_out, xor_2_out);
  or or_1 (or_1_out, and_1_out, and_2_out);
  and and_3 (and_3_out, not_1_out, d_ff_10_q);
  or or_2 (or_2_out, and_3_out, and_14_out);
  xor xor_1 (xor_1_out, or_2_out, xor_2_out);
  and and_4 (and_4_out, d_ff_3_q, or_5_out);
  or or_3 (or_3_out, and_4_out, and_6_out);
  xor xor_2 (xor_2_out, d_ff_2_q, or_3_out);
  D_Flip_Flop d_ff_3 (.D(in_1), .clk(clock_1_out), .Q(d_ff_3_q));  // open: Qn, preset, reset
  not not_2 (not_2_out, d_ff_1_q);
  and and_5 (and_5_out, not_2_out, d_ff_11_q);
  and and_6 (and_6_out, or_4_out, xor_4_out);
  D_Flip_Flop d_ff_4 (.D(xor_1_out), .clk(clock_1_out), .Q(out_13));  // open: Qn, preset, reset
  or or_4 (or_4_out, and_5_out, and_13_out);
  xor xor_3 (xor_3_out, or_4_out, xor_4_out);
  and and_7 (and_7_out, d_ff_6_q, and_10_out);
  xor xor_4 (xor_4_out, d_ff_3_q, or_5_out);
  not not_3 (not_3_out, d_ff_1_q);
  and and_8 (and_8_out, or_6_out, xor_6_out);
  or or_5 (or_5_out, and_7_out, and_8_out);
  D_Flip_Flop d_ff_5 (.D(xor_3_out), .clk(clock_1_out), .Q(out_14));  // open: Qn, preset, reset
  D_Flip_Flop d_ff_6 (.D(left_input), .clk(clock_1_out), .Q(d_ff_6_q));  // open: Qn, preset, reset
  and and_9 (and_9_out, not_3_out, d_ff_12_q);
  or or_6 (or_6_out, and_9_out, and_12_out);
  xor xor_5 (xor_5_out, or_6_out, xor_6_out);
  or or_7 (or_7_out, d_ff_13_q, and_11_out);
  and and_10 (and_10_out, d_ff_8_q, or_7_out);
  xor xor_6 (xor_6_out, d_ff_6_q, and_10_out);
  D_Flip_Flop d_ff_7 (.D(xor_5_out), .clk(clock_1_out), .Q(out_15));  // open: Qn, preset, reset
  D_Flip_Flop d_ff_8 (.D(in_3), .clk(clock_1_out), .Q(d_ff_8_q));  // open: Qn, preset, reset
  or or_8 (or_8_out, d_ff_13_q, and_11_out);
  xor xor_7 (xor_7_out, d_ff_8_q, or_8_out);
  D_Flip_Flop d_ff_9 (.D(xor_7_out), .clk(clock_1_out), .Q(out_16));  // open: Qn, preset, reset
  and and_11 (and_11_out, d_ff_1_q, xor_11_out);
  and and_12 (and_12_out, d_ff_1_q, xor_10_out);
  and and_13 (and_13_out, d_ff_1_q, xor_9_out);
  and and_14 (and_14_out, d_ff_1_q, xor_8_out);
  D_Flip_Flop d_ff_10 (.D(in_4), .clk(clock_1_out), .Q(d_ff_10_q));  // open: Qn, preset, reset
  not not_4 (not_4_out, d_ff_10_q);
  xor xor_8 (xor_8_out, not_4_out, and_15_out);
  D_Flip_Flop d_ff_11 (.D(in_5), .clk(clock_1_out), .Q(d_ff_11_q));  // open: Qn, preset, reset
  and and_15 (and_15_out, not_5_out, and_16_out);
  not not_5 (not_5_out, d_ff_11_q);
  xor xor_9 (xor_9_out, not_5_out, and_16_out);
  D_Flip_Flop d_ff_12 (.D(in_6), .clk(clock_1_out), .Q(d_ff_12_q));  // open: Qn, preset, reset
  and and_16 (and_16_out, not_6_out, and_17_out);
  not not_6 (not_6_out, d_ff_12_q);
  xor xor_10 (xor_10_out, not_6_out, and_17_out);
  D_Flip_Flop d_ff_13 (.D(in_7), .clk(clock_1_out), .Q(d_ff_13_q));  // open: Qn, preset, reset
  and and_17 (and_17_out, d_ff_1_q, not_7_out);
  not not_7 (not_7_out, d_ff_13_q);
  xor xor_11 (xor_11_out, d_ff_1_q, not_7_out);
  not not_8 (not_8_out, xor_7_out);
  not not_9 (not_9_out, xor_5_out);
  and and_18 (and_18_out, not_8_out, not_9_out, not_10_out, not_11_out);
  not not_10 (not_10_out, xor_3_out);
  not not_11 (not_11_out, xor_1_out);
  not not_12 (not_12_out, d_ff_1_q);
  and and_19 (and_19_out, not_12_out, or_1_out);
  D_Flip_Flop d_ff_14 (.D(xor_1_out), .clk(clock_1_out), .Q(out_10));  // open: Qn, preset, reset
  D_Flip_Flop d_ff_15 (.D(and_18_out), .clk(clock_1_out), .Q(out_11));  // open: Qn, preset, reset
  D_Flip_Flop d_ff_16 (.D(and_19_out), .clk(clock_1_out), .Q(out_12));  // open: Qn, preset, reset

  // Notes on the sheet:
  //   Samuel Kinyua
  //   261074364
  //   Add/Sub command
  //   A-out pins
  //   right input
  //   Negative
  //   zero
  //   Overflow
  //   Status output
endmodule
