// Logisim project project.circ as structural Verilog: 1 circuit, main circuit main
module main (
  input  in_1,
  input  in_2,
  input  in_3,
  input  in_4,
  output out_5,
  output out_6,
  output out_7
);

  wire and_1_out, and_2_out, and_3_out, and_4_out, and_5_out, and_6_out, and_7_out, and_8_out, and_9_out,
       and_10_out, and_11_out, and_12_out, and_13_out, and_14_out, and_15_out, and_16_out, and_17_out,
       and_18_out, and_19_out, and_20_out, and_21_out, and_22_out, and_23_out, and_24_out, and_25_out,
       and_26_out, and_27_out, and_28_out, and_29_out, and_30_out, and_31_out, and_32_out, and_33_out,
       and_34_out, and_35_out, and_36_out, and_37_out, and_38_out, and_39_out, and_40_out, and_41_out,
       and_42_out, and_43_out, and_44_out, and_45_out, and_46_out, and_47_out, and_48_out, and_49_out,
       and_50_out, and_51_out, and_52_out, and_53_out, and_54_out, and_55_out, and_56_out, and_57_out,
       and_58_out, and_59_out, and_60_out, and_61_out, and_62_out, and_63_out, and_64_out, and_65_out,
       and_66_out, and_67_out, and_68_out, and_69_out, and_70_out, and_71_out, and_72_out, and_73_out,
       and_74_out, and_75_out, and_76_out, and_77_out, and_78_out, and_79_out, and_80_out, and_81_out,
       and_82_out, and_83_out, and_84_out, and_85_out, and_86_out, and_87_out, and_88_out, and_89_out,
       and_90_out, and_91_out, and_92_out, and_93_out, and_94_out, and_95_out, and_96_out, and_97_out,
       and_98_out, and_99_out, and_100_out, and_101_out, and_102_out, and_103_out, and_104_out, and_105_out,
       and_106_out, and_107_out, and_108_out, and_109_out, and_110_out, and_111_out, and_112_out,
       and_113_out, and_114_out, and_115_out, and_116_out, and_117_out, and_118_out, and_119_out,
       and_120_out, and_121_out, and_122_out, and_123_out, and_124_out, and_125_out, and_126_out,
       and_127_out, and_128_out, and_129_out, and_130_out, and_131_out, and_132_out, and_133_out,
       and_134_out, and_135_out, and_136_out, and_138_out, clock_1_out, d_ff_1_q, d_ff_2_q, d_ff_3_q,
       d_ff_4_q, d_ff_5_q, d_ff_9_q, d_ff_10_q, d_ff_11_q, d_ff_12_q, d_ff_13_q, d_ff_14_q, d_ff_15_q,
       d_ff_16_q, d_ff_17_q, d_ff_18_q, d_ff_19_q, d_ff_20_q, d_ff_21_q, d_ff_22_q, d_ff_23_q, d_ff_24_q,
       d_ff_25_q, d_ff_26_q, d_ff_27_q, d_ff_29_q, d_ff_30_q, d_ff_31_q, d_ff_32_q, d_ff_33_q, d_ff_34_q,
       d_ff_35_q, d_ff_36_q, d_ff_37_q, d_ff_38_q, d_ff_39_q, d_ff_40_q, d_ff_41_q, d_ff_42_q, d_ff_43_q,
       d_ff_44_q, d_ff_45_q, d_ff_46_q, d_ff_47_q, d_ff_48_q, d_ff_49_q, d_ff_50_q, d_ff_51_q, d_ff_52_q,
       d_ff_53_q, d_ff_54_q, d_ff_55_q, d_ff_56_q, d_ff_57_q, d_ff_58_q, d_ff_59_q, d_ff_60_q, d_ff_61_q,
       d_ff_62_q, d_ff_63_q, d_ff_64_q, d_ff_65_q, d_ff_66_q, d_ff_67_q, d_ff_68_q, d_ff_69_q, d_ff_70_q,
       d_ff_71_q, d_ff_72_q, d_ff_73_q, d_ff_74_q, d_ff_75_q, d_ff_76_q, d_ff_77_q, d_ff_78_q, d_ff_79_q,
       d_ff_80_q, d_ff_81_q, d_ff_82_q, d_ff_83_q, decoder_1_out0, decoder_1_out1, decoder_1_out2,
       decoder_1_out3, decoder_1_out4, decoder_1_out5, decoder_1_out6, decoder_1_out7, not_1_out, not_2_out,
       not_3_out, not_4_out, not_5_out, not_6_out, not_7_out, not_8_out, or_1_out, or_2_out, or_3_out,
       or_4_out, or_5_out, or_6_out, or_7_out, or_8_out, or_9_out, or_11_out, or_12_out, or_13_out,
       or_14_out, or_15_out, or_16_out, or_17_out, or_18_out, or_19_out, or_20_out, or_21_out, or_22_out,
       or_23_out, or_24_out, or_25_out, or_26_out, or_27_out, or_28_out, or_29_out, or_30_out, or_31_out,
       or_32_out, or_33_out, or_34_out, xor_1_out, xor_2_out, xor_3_out, xor_4_out, xor_5_out, xor_6_out,
       xor_7_out, xor_8_out, xor_9_out, xor_10_out, xor_11_out, xor_12_out, xor_13_out, xor_14_out,
       xor_15_out;
  wire [2:0] d_ff_8_q;

  Clock #(.lowDuration(2)) clock_1 (.out(clock_1_out));
  and and_1 (and_1_out, d_ff_25_q, d_ff_46_q, d_ff_61_q, d_ff_80_q);
  or or_1 (or_1_out, and_3_out, and_4_out);
  or or_2 (or_2_out, and_5_out, and_6_out);
  or or_3 (or_3_out, and_7_out, and_8_out);
  or or_4 (or_4_out, and_9_out, and_10_out);
  D_Flip_Flop d_ff_1 (.D(and_1_out), .clk(clock_1_out), .Q(d_ff_1_q));  // open: Qn, preset, reset
  and and_2 (and_2_out, ~d_ff_4_q, ~d_ff_5_q);  // AND_Gate
  and and_3 (and_3_out, d_ff_25_q, and_63_out);
  and and_4 (and_4_out, ~d_ff_25_q, d_ff_29_q);  // AND_Gate
  and and_5 (and_5_out, d_ff_25_q, and_85_out);
  and and_6 (and_6_out, ~d_ff_25_q, d_ff_48_q);  // AND_Gate
  and and_7 (and_7_out, d_ff_25_q, and_108_out);
  and and_8 (and_8_out, ~d_ff_25_q, d_ff_64_q);  // AND_Gate
  and and_9 (and_9_out, d_ff_25_q, and_130_out);
  and and_10 (and_10_out, ~d_ff_25_q, d_ff_82_q);  // AND_Gate
  and and_11 (and_11_out, ~d_ff_4_q, d_ff_5_q);  // AND_Gate
  and and_12 (and_12_out, d_ff_4_q, ~d_ff_5_q);  // AND_Gate
  and and_13 (and_13_out, clock_1_out, ~d_ff_1_q);  // AND_Gate
  and and_14 (and_14_out, d_ff_46_q, ~d_ff_25_q);  // AND_Gate
  or or_5 (or_5_out, and_11_out, and_16_out);
  and and_15 (and_15_out, and_12_out, clock_1_out);
  and and_16 (and_16_out, d_ff_4_q, d_ff_5_q);
  D_Flip_Flop d_ff_2 (.D(d_ff_4_q), .clk(clock_1_out), .Q(d_ff_2_q));  // open: Qn, preset, reset
  and and_17 (and_17_out, clock_1_out, and_16_out);
  not not_1 (not_1_out, d_ff_61_q);
  D_Flip_Flop d_ff_3 (.D(d_ff_5_q), .clk(clock_1_out), .Q(d_ff_3_q));  // open: Qn, preset, reset
  and and_18 (and_18_out, d_ff_3_q, clock_1_out);
  xor xor_1 (xor_1_out, d_ff_2_q, and_18_out);
  D_Flip_Flop #(.trigger("falling")) d_ff_4 (
    .D(xor_1_out), .clk(clock_1_out), .Q(d_ff_4_q));  // open: Qn, preset, reset
  xor xor_2 (xor_2_out, d_ff_3_q, clock_1_out);
  and and_19 (and_19_out, d_ff_80_q, ~d_ff_25_q);  // AND_Gate
  D_Flip_Flop #(.trigger("falling")) d_ff_5 (
    .D(xor_2_out), .clk(clock_1_out), .Q(d_ff_5_q));  // open: Qn, preset, reset
  D_Flip_Flop d_ff_6 (.D(xor_3_out), .clk(and_13_out), .Q(d_ff_8_q[2]));  // open: Qn, preset, reset
  and and_20 (and_20_out, not_1_out, or_5_out, and_14_out, clock_1_out);
  or or_6 (or_6_out, and_19_out, d_ff_25_q);
  D_Flip_Flop d_ff_7 (.D(xor_4_out), .clk(and_13_out), .Q(d_ff_8_q[1]));  // open: Qn, preset, reset
  xor xor_3 (xor_3_out, d_ff_8_q[2], and_21_out);
  and and_21 (and_21_out, d_ff_8_q[1], and_23_out);
  and and_22 (and_22_out, d_ff_61_q, and_14_out, or_5_out, clock_1_out);
  D_Flip_Flop d_ff_8 (.D(xor_5_out), .clk(and_13_out), .Q(d_ff_8_q[0]));  // open: Qn, preset, reset
  xor xor_4 (xor_4_out, d_ff_8_q[1], and_24_out);
  and and_23 (and_23_out, d_ff_8_q[1], and_24_out);
  xor xor_5 (xor_5_out, d_ff_8_q[0], and_26_out);
  and and_24 (and_24_out, d_ff_8_q[0], and_26_out);
  and and_25 (and_25_out, d_ff_25_q, and_16_out, clock_1_out);
  and and_26 (and_26_out, ~d_ff_25_q, ~d_ff_46_q, ~d_ff_61_q, ~d_ff_80_q);  // AND_Gate
  or or_7 (or_7_out, and_22_out, and_25_out);
  and and_27 (and_27_out, or_6_out, d_ff_13_q);  // AND_Gate
  Decoder #(.select(3)) decoder_1 (
    .out0(decoder_1_out0), .out1(decoder_1_out1), .out2(decoder_1_out2), .out3(decoder_1_out3),
    .out4(decoder_1_out4), .out5(decoder_1_out5), .out6(decoder_1_out6), .out7(decoder_1_out7), .sel(d_ff_8_q));  // open: en
  and and_28 (and_28_out, ~or_6_out, d_ff_62_q);  // AND_Gate
  D_Flip_Flop d_ff_9 (.D(d_ff_46_q), .clk(and_17_out), .Q(d_ff_9_q));  // open: Qn, preset, reset
  D_Flip_Flop d_ff_10 (.D(or_6_out), .clk(and_17_out), .Q(d_ff_10_q));  // open: Qn, preset, reset
  not not_2 (not_2_out, d_ff_1_q);
  not not_3 (not_3_out, d_ff_10_q);
  D_Flip_Flop d_ff_11 (.D(d_ff_46_q), .clk(and_15_out), .Q(d_ff_11_q));  // open: Qn, preset, reset
  D_Flip_Flop d_ff_12 (.D(in_1), .clk(and_13_out), .Q(d_ff_12_q));  // open: Qn, preset, reset
  and and_29 (and_29_out, decoder_1_out0, and_13_out, ~not_2_out);  // AND_Gate
  and and_30 (and_30_out, decoder_1_out1, and_13_out, ~not_2_out);  // AND_Gate
  and and_31 (and_31_out, decoder_1_out2, and_13_out, ~not_2_out);  // AND_Gate
  and and_32 (and_32_out, decoder_1_out3, and_13_out, ~not_2_out);  // AND_Gate
  and and_33 (and_33_out, decoder_1_out4, and_13_out, ~not_2_out);  // AND_Gate
  and and_34 (and_34_out, decoder_1_out5, and_13_out, ~not_2_out);  // AND_Gate
  and and_35 (and_35_out, decoder_1_out6, and_13_out, ~not_2_out);  // AND_Gate
  and and_36 (and_36_out, decoder_1_out7, and_13_out, ~not_2_out);  // AND_Gate
  D_Flip_Flop #(.trigger("high")) d_ff_13 (.D(or_1_out), .clk(and_20_out), .Q(d_ff_13_q));  // open: Qn, preset, reset
  and and_37 (and_37_out, d_ff_25_q, d_ff_61_q, d_ff_62_q);
  and and_38 (and_38_out, d_ff_25_q, ~d_ff_61_q, d_ff_13_q);  // AND_Gate
  or or_8 (or_8_out, and_38_out, and_37_out);
  D_Flip_Flop #(.trigger("high")) d_ff_14 (.D(or_8_out), .clk(and_15_out), .Q(d_ff_14_q));  // open: Qn, preset, reset
  or or_9 (or_9_out, and_28_out, and_27_out);
  and and_39 (and_39_out, not_3_out, and_17_out, ~d_ff_9_q);  // AND_Gate
  and and_40 (and_40_out, d_ff_10_q, and_17_out, ~d_ff_9_q);  // AND_Gate
  D_Flip_Flop #(.trigger("falling")) d_ff_15 (
    .D(d_ff_12_q), .clk(and_29_out), .Q(d_ff_15_q));  // open: Qn, preset, reset
  D_Flip_Flop #(.trigger("falling")) d_ff_16 (
    .D(d_ff_12_q), .clk(and_30_out), .Q(d_ff_16_q));  // open: Qn, preset, reset
  D_Flip_Flop #(.trigger("falling")) d_ff_17 (
    .D(d_ff_12_q), .clk(and_31_out), .Q(d_ff_17_q));  // open: Qn, preset, reset
  D_Flip_Flop #(.trigger("falling")) d_ff_18 (
    .D(d_ff_12_q), .clk(and_32_out), .Q(d_ff_18_q));  // open: Qn, preset, reset
  D_Flip_Flop #(.trigger("falling")) d_ff_19 (
    .D(d_ff_12_q), .clk(and_33_out), .Q(d_ff_19_q));  // open: Qn, preset, reset
  D_Flip_Flop #(.trigger("falling")) d_ff_20 (
    .D(d_ff_12_q), .clk(and_34_out), .Q(d_ff_20_q));  // open: Qn, preset, reset
  D_Flip_Flop #(.trigger("falling")) d_ff_21 (
    .D(d_ff_12_q), .clk(and_35_out), .Q(d_ff_21_q));  // open: Qn, preset, reset
  D_Flip_Flop #(.trigger("falling")) d_ff_22 (
    .D(d_ff_12_q), .clk(and_36_out), .Q(d_ff_22_q));  // open: Qn, preset, reset
  and and_41 (and_41_out, not_2_out, and_2_out, and_13_out);
  and and_42 (and_42_out, d_ff_25_q, ~d_ff_61_q, d_ff_26_q);  // AND_Gate
  xor xor_6 (xor_6_out, d_ff_14_q, or_22_out);
  and and_43 (and_43_out, d_ff_14_q, or_22_out);
  and and_44 (and_44_out, xor_6_out, or_14_out);
  or or_10 (out_7, and_43_out, and_44_out);
  and and_45 (and_45_out, or_6_out, d_ff_26_q);  // AND_Gate
  D_Flip_Flop #(.trigger("high")) d_ff_23 (.D(or_9_out), .clk(and_39_out), .Q(d_ff_23_q));  // open: Qn, preset, reset
  D_Flip_Flop #(.trigger("high")) d_ff_24 (.D(or_9_out), .clk(and_40_out), .Q(d_ff_24_q));  // open: Qn, preset, reset
  and and_46 (and_46_out, d_ff_9_q, and_17_out);
  and and_47 (and_47_out, not_2_out, or_12_out);
  D_Flip_Flop #(.trigger("high")) d_ff_25 (.D(and_47_out), .clk(and_41_out), .Q(d_ff_25_q));  // open: Qn, preset, reset
  D_Flip_Flop #(.trigger("high")) d_ff_26 (.D(or_2_out), .clk(and_20_out), .Q(d_ff_26_q));  // open: Qn, preset, reset
  and and_48 (and_48_out, d_ff_25_q, d_ff_61_q, d_ff_67_q);
  or or_11 (or_11_out, and_42_out, and_48_out);
  D_Flip_Flop #(.trigger("high")) d_ff_27 (.D(or_11_out), .clk(and_15_out), .Q(d_ff_27_q));  // open: Qn, preset, reset
  xor xor_7 (xor_7_out, xor_6_out, or_14_out);
  D_Flip_Flop #(.trigger("falling")) d_ff_28 (.D(xor_7_out), .clk(and_15_out), .Q(out_5));  // open: Qn, preset, reset
  and and_49 (and_49_out, ~or_6_out, d_ff_67_q);  // AND_Gate
  and and_50 (and_50_out, d_ff_24_q, d_ff_10_q);
  and and_51 (and_51_out, d_ff_9_q, or_16_out);
  D_Flip_Flop #(.trigger("high")) d_ff_29 (.D(and_51_out), .clk(and_46_out), .Q(d_ff_29_q));  // open: Qn, preset, reset
  D_Flip_Flop d_ff_30 (.D(in_2), .clk(and_13_out), .Q(d_ff_30_q));  // open: Qn, preset, reset
  and and_52 (and_52_out, d_ff_15_q, decoder_1_out0);
  and and_53 (and_53_out, d_ff_16_q, decoder_1_out1);
  and and_54 (and_54_out, d_ff_17_q, decoder_1_out2);
  and and_55 (and_55_out, d_ff_18_q, decoder_1_out3);
  and and_56 (and_56_out, d_ff_19_q, decoder_1_out4);
  and and_57 (and_57_out, d_ff_20_q, decoder_1_out5);
  and and_58 (and_58_out, d_ff_21_q, decoder_1_out6);
  and and_59 (and_59_out, d_ff_22_q, decoder_1_out7);
  or or_12 (or_12_out, and_59_out, and_58_out, and_57_out, and_56_out, and_55_out, and_54_out, and_53_out, and_52_out);
  and and_60 (and_60_out, d_ff_25_q, ~d_ff_61_q, d_ff_31_q);  // AND_Gate
  or or_13 (or_13_out, and_60_out, and_65_out);
  xor xor_8 (xor_8_out, d_ff_27_q, or_24_out);
  and and_61 (and_61_out, d_ff_27_q, or_24_out);
  and and_62 (and_62_out, xor_8_out, or_18_out);
  or or_14 (or_14_out, and_61_out, and_62_out);
  and and_63 (and_63_out, out_5, d_ff_25_q);
  or or_15 (or_15_out, and_49_out, and_45_out);
  and and_64 (and_64_out, d_ff_23_q, not_3_out);
  or or_16 (or_16_out, and_50_out, and_64_out);
  D_Flip_Flop #(.trigger("high")) d_ff_31 (.D(or_3_out), .clk(and_20_out), .Q(d_ff_31_q));  // open: Qn, preset, reset
  and and_65 (and_65_out, d_ff_25_q, d_ff_61_q, d_ff_78_q);
  D_Flip_Flop #(.trigger("high")) d_ff_32 (.D(or_13_out), .clk(and_15_out), .Q(d_ff_32_q));  // open: Qn, preset, reset
  and and_66 (and_66_out, d_ff_32_q, or_26_out);
  xor xor_9 (xor_9_out, xor_8_out, or_18_out);
  D_Flip_Flop #(.trigger("falling")) d_ff_33 (
    .D(xor_9_out), .clk(and_15_out), .Q(d_ff_33_q));  // open: Qn, preset, reset
  D_Flip_Flop #(.trigger("falling")) d_ff_34 (
    .D(d_ff_30_q), .clk(and_29_out), .Q(d_ff_34_q));  // open: Qn, preset, reset
  D_Flip_Flop #(.trigger("falling")) d_ff_35 (
    .D(d_ff_30_q), .clk(and_30_out), .Q(d_ff_35_q));  // open: Qn, preset, reset
  D_Flip_Flop #(.trigger("falling")) d_ff_36 (
    .D(d_ff_30_q), .clk(and_31_out), .Q(d_ff_36_q));  // open: Qn, preset, reset
  D_Flip_Flop #(.trigger("falling")) d_ff_37 (
    .D(d_ff_30_q), .clk(and_32_out), .Q(d_ff_37_q));  // open: Qn, preset, reset
  D_Flip_Flop #(.trigger("falling")) d_ff_38 (
    .D(d_ff_30_q), .clk(and_33_out), .Q(d_ff_38_q));  // open: Qn, preset, reset
  D_Flip_Flop #(.trigger("falling")) d_ff_39 (
    .D(d_ff_30_q), .clk(and_34_out), .Q(d_ff_39_q));  // open: Qn, preset, reset
  D_Flip_Flop #(.trigger("falling")) d_ff_40 (
    .D(d_ff_30_q), .clk(and_35_out), .Q(d_ff_40_q));  // open: Qn, preset, reset
  D_Flip_Flop #(.trigger("falling")) d_ff_41 (
    .D(d_ff_30_q), .clk(and_36_out), .Q(d_ff_41_q));  // open: Qn, preset, reset
  and and_67 (and_67_out, not_2_out, and_2_out, and_13_out);
  D_Flip_Flop #(.trigger("high")) d_ff_42 (.D(or_4_out), .clk(and_20_out), .Q(d_ff_42_q));  // open: Qn, preset, reset
  and and_68 (and_68_out, d_ff_25_q, ~d_ff_61_q, d_ff_42_q);  // AND_Gate
  and and_69 (and_69_out, d_ff_25_q, d_ff_61_q, d_ff_83_q);
  or or_17 (or_17_out, and_68_out, and_69_out);
  D_Flip_Flop #(.trigger("high")) d_ff_43 (.D(or_17_out), .clk(and_15_out), .Q(d_ff_43_q));  // open: Qn, preset, reset
  xor xor_10 (xor_10_out, d_ff_32_q, or_26_out);
  and and_70 (and_70_out, xor_10_out, and_74_out);
  or or_18 (or_18_out, and_66_out, and_70_out);
  and and_71 (and_71_out, or_6_out, d_ff_31_q);  // AND_Gate
  D_Flip_Flop #(.trigger("high")) d_ff_44 (.D(or_15_out), .clk(and_39_out), .Q(d_ff_44_q));  // open: Qn, preset, reset
  D_Flip_Flop #(.trigger("high")) d_ff_45 (.D(or_15_out), .clk(and_40_out), .Q(d_ff_45_q));  // open: Qn, preset, reset
  and and_72 (and_72_out, d_ff_9_q, and_17_out);
  and and_73 (and_73_out, not_2_out, or_21_out);
  D_Flip_Flop #(.trigger("high")) d_ff_46 (.D(and_73_out), .clk(and_67_out), .Q(d_ff_46_q));  // open: Qn, preset, reset
  and and_74 (and_74_out, d_ff_43_q, or_29_out);
  xor xor_11 (xor_11_out, xor_10_out, and_74_out);
  D_Flip_Flop #(.trigger("falling")) d_ff_47 (
    .D(xor_11_out), .clk(and_15_out), .Q(d_ff_47_q));  // open: Qn, preset, reset
  and and_75 (and_75_out, ~or_6_out, d_ff_78_q);  // AND_Gate
  and and_76 (and_76_out, d_ff_9_q, or_20_out);
  D_Flip_Flop #(.trigger("high")) d_ff_48 (.D(and_76_out), .clk(and_72_out), .Q(d_ff_48_q));  // open: Qn, preset, reset
  and and_77 (and_77_out, d_ff_34_q, decoder_1_out0);
  and and_78 (and_78_out, d_ff_35_q, decoder_1_out1);
  and and_79 (and_79_out, d_ff_36_q, decoder_1_out2);
  and and_80 (and_80_out, d_ff_37_q, decoder_1_out3);
  and and_81 (and_81_out, d_ff_38_q, decoder_1_out4);
  and and_82 (and_82_out, d_ff_39_q, decoder_1_out5);
  and and_83 (and_83_out, d_ff_40_q, decoder_1_out6);
  and and_84 (and_84_out, d_ff_41_q, decoder_1_out7);
  xor xor_12 (xor_12_out, d_ff_43_q, or_29_out);
  and and_85 (and_85_out, d_ff_33_q, d_ff_25_q);
  or or_19 (or_19_out, and_75_out, and_71_out);
  and and_86 (and_86_out, d_ff_44_q, not_3_out);
  and and_87 (and_87_out, d_ff_45_q, d_ff_10_q);
  or or_20 (or_20_out, and_87_out, and_86_out);
  D_Flip_Flop d_ff_49 (.D(in_3), .clk(and_13_out), .Q(d_ff_49_q));  // open: Qn, preset, reset
  or or_21 (or_21_out, and_84_out, and_83_out, and_82_out, and_81_out, and_80_out, and_79_out, and_78_out, and_77_out);
  and and_88 (and_88_out, d_ff_63_q, ~d_ff_11_q);  // AND_Gate
  D_Flip_Flop #(.trigger("falling")) d_ff_50 (
    .D(xor_12_out), .clk(and_15_out), .Q(d_ff_50_q));  // open: Qn, preset, reset
  D_Flip_Flop #(.trigger("falling")) d_ff_51 (
    .D(d_ff_49_q), .clk(and_29_out), .Q(d_ff_51_q));  // open: Qn, preset, reset
  D_Flip_Flop #(.trigger("falling")) d_ff_52 (
    .D(d_ff_49_q), .clk(and_30_out), .Q(d_ff_52_q));  // open: Qn, preset, reset
  D_Flip_Flop #(.trigger("falling")) d_ff_53 (
    .D(d_ff_49_q), .clk(and_31_out), .Q(d_ff_53_q));  // open: Qn, preset, reset
  D_Flip_Flop #(.trigger("falling")) d_ff_54 (
    .D(d_ff_49_q), .clk(and_32_out), .Q(d_ff_54_q));  // open: Qn, preset, reset
  D_Flip_Flop #(.trigger("falling")) d_ff_55 (
    .D(d_ff_49_q), .clk(and_33_out), .Q(d_ff_55_q));  // open: Qn, preset, reset
  D_Flip_Flop #(.trigger("falling")) d_ff_56 (
    .D(d_ff_49_q), .clk(and_34_out), .Q(d_ff_56_q));  // open: Qn, preset, reset
  D_Flip_Flop #(.trigger("falling")) d_ff_57 (
    .D(d_ff_49_q), .clk(and_35_out), .Q(d_ff_57_q));  // open: Qn, preset, reset
  D_Flip_Flop #(.trigger("falling")) d_ff_58 (
    .D(d_ff_49_q), .clk(and_36_out), .Q(d_ff_58_q));  // open: Qn, preset, reset
  and and_89 (and_89_out, not_2_out, and_2_out, and_13_out);
  and and_90 (and_90_out, d_ff_66_q, ~d_ff_11_q);  // AND_Gate
  or or_22 (or_22_out, and_88_out, and_129_out);
  D_Flip_Flop #(.trigger("high")) d_ff_59 (.D(or_19_out), .clk(and_39_out), .Q(d_ff_59_q));  // open: Qn, preset, reset
  D_Flip_Flop #(.trigger("high")) d_ff_60 (.D(or_19_out), .clk(and_40_out), .Q(d_ff_60_q));  // open: Qn, preset, reset
  and and_91 (and_91_out, d_ff_9_q, and_17_out);
  and and_92 (and_92_out, not_2_out, or_25_out);
  and and_93 (and_93_out, d_ff_25_q, ~d_ff_80_q, d_ff_13_q);  // AND_Gate
  or or_23 (or_23_out, and_93_out, and_106_out);
  and and_94 (and_94_out, d_ff_79_q, ~d_ff_11_q);  // AND_Gate
  or or_24 (or_24_out, and_90_out, and_135_out);
  and and_95 (and_95_out, or_6_out, d_ff_42_q);  // AND_Gate
  and and_96 (and_96_out, d_ff_9_q, or_27_out);
  and and_97 (and_97_out, d_ff_51_q, decoder_1_out0);
  and and_98 (and_98_out, d_ff_52_q, decoder_1_out1);
  and and_99 (and_99_out, d_ff_53_q, decoder_1_out2);
  and and_100 (and_100_out, d_ff_54_q, decoder_1_out3);
  and and_101 (and_101_out, d_ff_55_q, decoder_1_out4);
  and and_102 (and_102_out, d_ff_56_q, decoder_1_out5);
  and and_103 (and_103_out, d_ff_57_q, decoder_1_out6);
  and and_104 (and_104_out, d_ff_58_q, decoder_1_out7);
  or or_25 (or_25_out, and_104_out, and_103_out, and_102_out, and_101_out, and_100_out, and_99_out, and_98_out, and_97_out);
  D_Flip_Flop #(.trigger("high")) d_ff_61 (.D(and_92_out), .clk(and_89_out), .Q(d_ff_61_q));  // open: Qn, preset, reset
  D_Flip_Flop #(.trigger("high")) d_ff_62 (.D(or_1_out), .clk(or_7_out), .Q(d_ff_62_q));  // open: Qn, preset, reset
  and and_105 (and_105_out, d_ff_25_q, ~d_ff_80_q, d_ff_26_q);  // AND_Gate
  and and_106 (and_106_out, d_ff_25_q, d_ff_80_q, d_ff_62_q);
  D_Flip_Flop #(.trigger("high")) d_ff_63 (.D(or_23_out), .clk(and_15_out), .Q(d_ff_63_q));  // open: Qn, preset, reset
  and and_107 (and_107_out, d_ff_81_q, ~d_ff_11_q);  // AND_Gate
  or or_26 (or_26_out, and_94_out, and_136_out);
  and and_108 (and_108_out, d_ff_47_q, d_ff_25_q);
  and and_109 (and_109_out, ~or_6_out, d_ff_83_q);  // AND_Gate
  and and_110 (and_110_out, d_ff_59_q, not_3_out);
  and and_111 (and_111_out, d_ff_60_q, d_ff_10_q);
  or or_27 (or_27_out, and_111_out, and_110_out);
  D_Flip_Flop #(.trigger("high")) d_ff_64 (.D(and_96_out), .clk(and_91_out), .Q(d_ff_64_q));  // open: Qn, preset, reset
  D_Flip_Flop d_ff_65 (.D(in_4), .clk(and_13_out), .Q(d_ff_65_q));  // open: Qn, preset, reset
  and and_112 (and_112_out, d_ff_25_q, d_ff_80_q, d_ff_67_q);
  or or_28 (or_28_out, and_105_out, and_112_out);
  D_Flip_Flop #(.trigger("high")) d_ff_66 (.D(or_28_out), .clk(and_15_out), .Q(d_ff_66_q));  // open: Qn, preset, reset
  or or_29 (or_29_out, and_107_out, and_138_out);
  or or_30 (or_30_out, and_109_out, and_95_out);
  D_Flip_Flop #(.trigger("high")) d_ff_67 (.D(or_2_out), .clk(or_7_out), .Q(d_ff_67_q));  // open: Qn, preset, reset
  and and_113 (and_113_out, d_ff_25_q, ~d_ff_80_q, d_ff_31_q);  // AND_Gate
  not not_4 (not_4_out, d_ff_63_q);
  D_Flip_Flop #(.trigger("high")) d_ff_68 (.D(or_30_out), .clk(and_39_out), .Q(d_ff_68_q));  // open: Qn, preset, reset
  D_Flip_Flop #(.trigger("high")) d_ff_69 (.D(or_30_out), .clk(and_40_out), .Q(d_ff_69_q));  // open: Qn, preset, reset
  and and_114 (and_114_out, d_ff_9_q, and_17_out);
  D_Flip_Flop #(.trigger("falling")) d_ff_70 (
    .D(d_ff_65_q), .clk(and_29_out), .Q(d_ff_70_q));  // open: Qn, preset, reset
  D_Flip_Flop #(.trigger("falling")) d_ff_71 (
    .D(d_ff_65_q), .clk(and_30_out), .Q(d_ff_71_q));  // open: Qn, preset, reset
  D_Flip_Flop #(.trigger("falling")) d_ff_72 (
    .D(d_ff_65_q), .clk(and_31_out), .Q(d_ff_72_q));  // open: Qn, preset, reset
  D_Flip_Flop #(.trigger("falling")) d_ff_73 (
    .D(d_ff_65_q), .clk(and_32_out), .Q(d_ff_73_q));  // open: Qn, preset, reset
  D_Flip_Flop #(.trigger("falling")) d_ff_74 (
    .D(d_ff_65_q), .clk(and_33_out), .Q(d_ff_74_q));  // open: Qn, preset, reset
  D_Flip_Flop #(.trigger("falling")) d_ff_75 (
    .D(d_ff_65_q), .clk(and_34_out), .Q(d_ff_75_q));  // open: Qn, preset, reset
  D_Flip_Flop #(.trigger("falling")) d_ff_76 (
    .D(d_ff_65_q), .clk(and_35_out), .Q(d_ff_76_q));  // open: Qn, preset, reset
  D_Flip_Flop #(.trigger("falling")) d_ff_77 (
    .D(d_ff_65_q), .clk(and_36_out), .Q(d_ff_77_q));  // open: Qn, preset, reset
  and and_115 (and_115_out, not_2_out, and_2_out, and_13_out);
  D_Flip_Flop #(.trigger("high")) d_ff_78 (.D(or_3_out), .clk(or_7_out), .Q(d_ff_78_q));  // open: Qn, preset, reset
  and and_116 (and_116_out, d_ff_25_q, d_ff_80_q, d_ff_78_q);
  or or_31 (or_31_out, and_113_out, and_116_out);
  D_Flip_Flop #(.trigger("high")) d_ff_79 (.D(or_31_out), .clk(and_15_out), .Q(d_ff_79_q));  // open: Qn, preset, reset
  xor xor_13 (xor_13_out, not_4_out, and_128_out);
  and and_117 (and_117_out, d_ff_9_q, or_33_out);
  and and_118 (and_118_out, d_ff_70_q, decoder_1_out0);
  and and_119 (and_119_out, d_ff_71_q, decoder_1_out1);
  and and_120 (and_120_out, d_ff_72_q, decoder_1_out2);
  and and_121 (and_121_out, d_ff_73_q, decoder_1_out3);
  and and_122 (and_122_out, d_ff_74_q, decoder_1_out4);
  and and_123 (and_123_out, d_ff_75_q, decoder_1_out5);
  and and_124 (and_124_out, d_ff_76_q, decoder_1_out6);
  and and_125 (and_125_out, d_ff_77_q, decoder_1_out7);
  and and_126 (and_126_out, not_2_out, or_34_out);
  D_Flip_Flop #(.trigger("high")) d_ff_80 (
    .D(and_126_out), .clk(and_115_out), .Q(d_ff_80_q));  // open: Qn, preset, reset
  and and_127 (and_127_out, d_ff_25_q, ~d_ff_80_q, d_ff_42_q);  // AND_Gate
  or or_32 (or_32_out, and_127_out, and_133_out);
  D_Flip_Flop #(.trigger("high")) d_ff_81 (.D(or_32_out), .clk(and_15_out), .Q(d_ff_81_q));  // open: Qn, preset, reset
  not not_5 (not_5_out, d_ff_66_q);
  and and_128 (and_128_out, not_5_out, and_134_out);
  and and_129 (and_129_out, xor_13_out, d_ff_11_q);
  and and_130 (and_130_out, d_ff_50_q, d_ff_25_q);
  and and_131 (and_131_out, d_ff_68_q, not_3_out);
  and and_132 (and_132_out, d_ff_69_q, d_ff_10_q);
  or or_33 (or_33_out, and_132_out, and_131_out);
  D_Flip_Flop #(.trigger("high")) d_ff_82 (
    .D(and_117_out), .clk(and_114_out), .Q(d_ff_82_q));  // open: Qn, preset, reset
  or or_34 (or_34_out, and_125_out, and_124_out, and_123_out, and_122_out, and_121_out, and_120_out, and_119_out, and_118_out);
  D_Flip_Flop #(.trigger("high")) d_ff_83 (.D(or_4_out), .clk(or_7_out), .Q(d_ff_83_q));  // open: Qn, preset, reset
  and and_133 (and_133_out, d_ff_25_q, d_ff_80_q, d_ff_83_q);
  not not_6 (not_6_out, d_ff_79_q);
  and and_134 (and_134_out, not_6_out, not_7_out);
  xor xor_14 (xor_14_out, not_5_out, and_134_out);
  and and_135 (and_135_out, xor_14_out, d_ff_11_q);
  not not_7 (not_7_out, d_ff_81_q);
  xor xor_15 (xor_15_out, not_6_out, not_7_out);
  and and_136 (and_136_out, xor_15_out, d_ff_11_q);
  and and_137 (out_6, ~out_5, ~d_ff_33_q, ~d_ff_47_q, ~d_ff_50_q);  // AND_Gate
  not not_8 (not_8_out, not_7_out);
  and and_138 (and_138_out, not_8_out, d_ff_11_q);

  // Notes on the sheet:
  //   Samuel Kinyua
  //   261074364
  //   Zachary Liu
  //   261086925
  //   0 - fetch
  //   1 - load
  //   2 - ALU
  //   HALT MACHINE
  //   3 - Save
  //   JUMP IF EMPTY
  //   PC
  //   L Input is R0, R1
  //   Output
  //   R0
  //   R0
  //   L-Input
  //   Mode Selector
  //   1 = subtract
  //   0 = add
  //   R1
  //   Op Code
  //   Function Code
  //   Output
  //   R Input is R0, R1
  //   Register
  //   R1
  //   Register/RAM (depends on OP Code
  //   IR
  //   R-Input
  //   A-Out
  //   Data RAM
  //   JUMP +1 0000
  //   HALT 1111
  //   Register Block
  //   Write from R1 to RAM 0  0010
  //   Read to R0 from RAM 0  0100
  //   Write from R0 to RAM 1 0001
  //   Read to R1 from RAM 1 0111
  //   Add R0 to R0 1000
  //   Subtract R0 from R1 1110
  //   Status Output:
  //   Bit 1: Negative
  //   Bit 2: Zero
  //   Bit 3: Overflow
  //   ALU
  //   Write 00
  //   Read 01
  //   Add 10
  //   Subtract 11
  //   IF FIRST DIGIT = 1, ACTIVATE THIS
  //   AUTO-SWITCH TO REGISTER 1
  //   0 FOR WRITE
  //   1 FOR READ
  //   0 = Load/Save
  //   1 = Arithmetic
endmodule
